// Logisim project Single_Cycle_Processor.circ as structural Verilog: 2 circuits, main circuit Single_Cycle_Processor
module Single_Cycle_Processor (
  input  Jump_Signal,
  input  Brach_Signal
);

  wire ALUSrc, MemRd, MemtoReg, MemWr, register_file_1_p4, RegSource, RegWr;
  wire [4:0] ImmL, instruction_spliter_1_rd, instruction_spliter_1_rs1, instruction_spliter_1_rs2,
       multiplexer_2_out;
  wire [10:0] ImmH, ImmU;
  wire [15:0] Imm16;
  wire [19:0] BranshPC, JumpPC, PC, pc_1_1_outpcplus1, Register_q;
  wire [31:0] ALUIn, ALUOut, data_memory_1_data_out, Extended, instruction_memory_1__32_bit_iinstruction, Rs1;

  Jump jump_1 (.Imm16(Imm16), .Rs1(Rs1), .Pc_jump(JumpPC), .initial_pc(PC));
  Multiplexer #(.select(2), .width(20), .enable("false")) multiplexer_1 (
    .in0({20{1'b0}}), .in1(BranshPC), .in2(JumpPC), .in3(pc_1_1_outpcplus1), .out(PC),
    .sel({Jump_Signal, Brach_Signal}));
  Register #(.width(20)) Register (.D(PC), .Q(Register_q), .clk(register_file_1_p4));  // open: en, clr
  PC_1 pc_1_1 (.Initial_Pc(Register_q), .OutPcPlus1(pc_1_1_outpcplus1));
  // Branch_pc branch_pc_1: pin names not known; wires that end beside it: PC, ImmL, ImmH, BranshPC
  Instruction_Memory instruction_memory_1 (
    .PC(Register_q), .Clk(register_file_1_p4),
    ._32_bit_iinstruction(instruction_memory_1__32_bit_iinstruction));  // open: Input_Data
  Instruction_Spliter instruction_spliter_1 (
    .in_1(instruction_memory_1__32_bit_iinstruction), .RD(instruction_spliter_1_rd), .ImmL(ImmL),
    .Rs1(instruction_spliter_1_rs1), .Rs2(instruction_spliter_1_rs2), .ImmU(ImmU), .Imm16(Imm16));  // open: Opcode, F
  Multiplexer #(.width(5), .enable("false")) multiplexer_2 (
    .in0(instruction_spliter_1_rs1), .in1(instruction_spliter_1_rd), .out(multiplexer_2_out), .sel(RegSource));
  // Register_File register_file_1: pin names not known; wires that end beside it: multiplexer_2_out, instruction_spliter_1_rs2, instruction_spliter_1_rd, register_file_1_p4, RegWr
  Multiplexer #(.width(32), .enable("false")) multiplexer_3 (.in0(Extended), .out(ALUIn), .sel(ALUSrc));  // open: in1
  Data_Memory data_memory_1 (
    .Memory_Write(MemWr), .Clock(register_file_1_p4), .Data_Out(data_memory_1_data_out), .Memory_Read(MemRd));  // open: Address, Data_In
  Multiplexer #(.width(32), .enable("false")) multiplexer_4 (
    .in0(ALUOut), .in1(data_memory_1_data_out), .out(ALUIn), .sel(MemtoReg));
endmodule

module Instruction_Spliter (
  input  [31:0] in_1,
  output [5:0] Opcode,
  output [4:0] RD,
  output [4:0] ImmL,
  output [4:0] Rs1,
  output [15:0] Imm16,
  output [10:0] F,
  output [10:0] ImmU,
  output [4:0] Rs2
);

  Register #(.width(32)) register_1 (.D(in_1), .Q({F, Imm16[4:0], Rs1, ImmL, Opcode}));  // open: en, clk, clr

  assign Imm16[15:5] = F;
  assign ImmU = F;
  assign RD = ImmL;
  assign Rs2 = Imm16[4:0];

  // Notes on the sheet:
  //   SB_Type
  //   R_Tube
  //   I-Type
endmodule
